// Logisim project Conversor ASCII Para Braile.circ as structural Verilog: 5 circuits, main circuit Main
module Main (
  input  _1
);

  wire clock_1_out, codificador_de_32_letras_1_out_2, counter_1_carry, not_1_out, registrador_de_letra_1__6,
       registrador_de_letra_1__7, registrador_de_letra_1_out_4, registrador_de_letra_1_out_5,
       registrador_de_letra_1_out_7, registrador_de_letra_1_out_9;
  wire [4:0] conversor_8x5_1_out_2, counter_1_q;
  wire [6:0] rom_1_data;

  Counter #(.width(5), .max('h1f)) counter_1 (
    .Q(counter_1_q), .carry(counter_1_carry), .clk(clock_1_out), .clr(not_1_out));  // open: load, D, count
  Clock clock_1 (.out(clock_1_out));
  not not_1 (not_1_out, _1);
  ROM #(.addrWidth(5), .dataWidth(7)) rom_1 (.addr(counter_1_q), .data(rom_1_data), .sel(_1));
  Conversor_8X5 conversor_8x5_1 (.in_1(rom_1_data), .out_2(conversor_8x5_1_out_2));
  LED led_1 (.in(registrador_de_letra_1_out_4));
  LED led_2 (.in(registrador_de_letra_1__6));
  LED led_3 (.in(registrador_de_letra_1__7));
  Registrador_De_Letra registrador_de_letra_1 (
    .out_5(registrador_de_letra_1_out_5), .out_7(registrador_de_letra_1_out_7),
    .Entrada(conversor_8x5_1_out_2), .Clock(codificador_de_32_letras_1_out_2), .Reset(not_1_out),
    .out_4(registrador_de_letra_1_out_4), ._6(registrador_de_letra_1__6), ._7(registrador_de_letra_1__7),
    .out_9(registrador_de_letra_1_out_9));
  Codificador_De_32_Letras codificador_de_32_letras_1 (.in_1(counter_1_q), .out_2(codificador_de_32_letras_1_out_2));
  LED led_4 (.in(registrador_de_letra_1_out_9));
  LED led_5 (.in(registrador_de_letra_1_out_7));
  LED led_6 (.in(counter_1_carry));
  LED led_7 (.in(registrador_de_letra_1_out_5));

  // Notes on the sheet:
  //   3
  //   2
  //   Clock
  //   4
  //   On/off
  //   5
  //   9
  //   6
  //   7
  //   8
  //   10
  //   Recomeço da frase
endmodule

module Letras_LED (
  input  A,
  input  B,
  input  C,
  input  D,
  input  E,
  output L0,
  output L1,
  output L2,
  output L3,
  output L4,
  output L5
);

  wire nand_1_out, nand_2_out, nand_3_out, nand_4_out, nand_5_out, nand_6_out, nand_7_out, nand_8_out,
       nand_9_out, nand_10_out, nand_11_out, nand_12_out, nand_13_out, nand_14_out, nand_15_out, nand_16_out,
       nand_17_out, nand_18_out, nand_19_out, nand_20_out, nand_21_out, nand_22_out, nand_23_out,
       nand_24_out, nand_25_out, nand_26_out, nand_27_out, nand_28_out, nand_29_out, nand_30_out,
       nand_31_out, nand_32_out, nand_33_out, nand_34_out, nand_35_out, nand_36_out, nand_37_out,
       nand_38_out, nand_39_out, nand_40_out, nand_41_out, nand_42_out, nand_43_out, nand_44_out,
       nand_45_out, nand_46_out, nand_47_out, nand_48_out, nand_49_out, nand_50_out, nand_51_out,
       nand_52_out, nand_53_out, nand_54_out, nand_55_out, nand_56_out, nand_57_out, nand_58_out,
       nand_59_out, nand_60_out, nand_61_out, nand_62_out, nand_63_out, nand_64_out, nand_65_out,
       nand_66_out, nand_67_out, nand_68_out, nand_69_out, nand_70_out, nand_71_out, nand_72_out,
       nand_73_out, nand_74_out, nand_75_out, nand_76_out, nand_77_out, nand_78_out, nand_79_out,
       nand_80_out, nand_81_out, nand_82_out, nand_83_out, nand_84_out, nand_85_out, nand_86_out,
       nand_87_out, nand_88_out, nand_89_out, nand_90_out, nand_91_out, nand_92_out, nand_93_out,
       nand_94_out, nand_95_out, nand_96_out, nand_97_out, nand_98_out, nand_99_out, nand_100_out,
       nand_101_out, nand_102_out, nand_103_out, nand_104_out, nand_105_out, nand_106_out, nand_107_out,
       nand_108_out, nand_109_out, nand_110_out, nand_111_out, nand_112_out, nand_113_out, nand_114_out,
       nand_115_out, nand_116_out, nand_117_out, nand_118_out, nand_119_out, nand_120_out, nand_121_out,
       nand_122_out, nand_123_out, nand_124_out, nand_125_out, nand_126_out, nand_127_out, nand_128_out,
       nand_129_out, nand_130_out, nand_131_out, nand_132_out, nand_133_out, nand_134_out, nand_135_out,
       nand_136_out, nand_137_out, nand_138_out, nand_139_out, nand_140_out, nand_141_out, nand_142_out,
       nand_143_out, nand_144_out, nand_145_out, nand_146_out, nand_147_out, nand_148_out, nand_149_out,
       nand_150_out, nand_151_out, nand_152_out, nand_153_out, nand_154_out, nand_155_out, nand_156_out,
       nand_157_out, nand_158_out, nand_159_out, nand_160_out, nand_161_out, nand_162_out, nand_163_out,
       nand_164_out, nand_165_out, nand_166_out, nand_167_out, nand_168_out, nand_169_out, nand_170_out,
       nand_171_out, nand_172_out, nand_173_out, nand_174_out, nand_175_out, nand_176_out, nand_177_out,
       nand_178_out, nand_179_out, nand_180_out, nand_181_out, nand_182_out, nand_183_out, nand_184_out,
       nand_185_out, nand_186_out, nand_187_out, nand_188_out, nand_189_out, nand_190_out, nand_191_out,
       nand_192_out, nand_193_out, nand_194_out, nand_195_out, nand_196_out, nand_197_out, nand_198_out,
       nand_199_out, nand_200_out, nand_201_out, nand_202_out, nand_203_out, nand_204_out, nand_205_out,
       nand_206_out, nand_207_out, nand_208_out, nand_209_out, nand_210_out, nand_211_out, nand_212_out,
       nand_213_out, nand_214_out, nand_215_out, nand_216_out, nand_217_out, nand_218_out, nand_219_out,
       nand_220_out, nand_221_out, nand_222_out, nand_223_out, nand_224_out, nand_225_out, nand_226_out,
       nand_227_out, nand_228_out, nand_229_out, nand_230_out, nand_231_out, nand_232_out, nand_233_out,
       nand_234_out, nand_236_out, nand_237_out, nand_238_out, nand_239_out, nand_240_out, nand_241_out,
       nand_242_out, nand_243_out, nand_244_out, nand_245_out, nand_246_out, nand_247_out, nand_248_out,
       nand_249_out, nand_251_out, nand_252_out, nand_253_out, nand_254_out;

  nand nand_1 (nand_1_out, B, B);
  nand nand_2 (nand_2_out, D, D);
  nand nand_3 (nand_3_out, B, B);
  nand nand_4 (nand_4_out, A, A);
  nand nand_5 (nand_5_out, C, C);
  nand nand_6 (nand_6_out, D, D);
  nand nand_7 (nand_7_out, E, E);
  nand nand_8 (nand_8_out, C, C);
  nand nand_9 (nand_9_out, A, A);
  nand nand_10 (nand_10_out, C, C);
  nand nand_11 (nand_11_out, E, E);
  nand nand_12 (nand_12_out, B, B);
  nand nand_13 (nand_13_out, A, A);
  nand nand_14 (nand_14_out, D, D);
  nand nand_15 (nand_15_out, E, E);
  nand nand_16 (nand_16_out, B, B);
  nand nand_17 (nand_17_out, B, D);
  nand nand_18 (nand_18_out, B, D);
  nand nand_19 (nand_19_out, B, D);
  nand nand_20 (nand_20_out, B, D);
  nand nand_21 (nand_21_out, B, D);
  nand nand_22 (nand_22_out, B, D);
  nand nand_23 (nand_23_out, B, D);
  nand nand_24 (nand_24_out, B, D);
  nand nand_25 (nand_25_out, B, B);
  nand nand_26 (nand_26_out, A, A);
  nand nand_27 (nand_27_out, B, B);
  nand nand_28 (nand_28_out, E, E);
  nand nand_29 (nand_29_out, D, D);
  nand nand_30 (nand_30_out, A, A);
  nand nand_31 (nand_31_out, E, E);
  nand nand_32 (nand_32_out, A, A);
  nand nand_33 (nand_33_out, B, B);
  nand nand_34 (nand_34_out, D, D);
  nand nand_35 (nand_35_out, B, B);
  nand nand_36 (nand_36_out, D, D);
  nand nand_37 (nand_37_out, E, E);
  nand nand_38 (nand_38_out, A, A);
  nand nand_39 (nand_39_out, C, C);
  nand nand_40 (nand_40_out, E, E);
  nand nand_41 (nand_41_out, C, C);
  nand nand_42 (nand_42_out, D, D);
  nand nand_43 (nand_43_out, A, C);
  nand nand_44 (nand_44_out, A, C);
  nand nand_45 (nand_45_out, A, C);
  nand nand_46 (nand_46_out, A, C);
  nand nand_47 (nand_47_out, A, C);
  nand nand_48 (nand_48_out, A, C);
  nand nand_49 (nand_49_out, A, C);
  nand nand_50 (nand_50_out, A, C);
  nand nand_51 (nand_51_out, nand_1_out, nand_2_out);
  nand nand_52 (nand_52_out, nand_3_out, D);
  nand nand_53 (nand_53_out, nand_4_out, D);
  nand nand_54 (nand_54_out, B, nand_5_out);
  nand nand_55 (nand_55_out, nand_6_out, nand_7_out);
  nand nand_56 (nand_56_out, A, nand_8_out);
  nand nand_57 (nand_57_out, nand_9_out, nand_10_out);
  nand nand_58 (nand_58_out, D, nand_11_out);
  nand nand_59 (nand_59_out, nand_12_out, C);
  nand nand_60 (nand_60_out, nand_13_out, B);
  nand nand_61 (nand_61_out, nand_14_out, nand_15_out);
  nand nand_62 (nand_62_out, A, nand_16_out);
  nand nand_63 (nand_63_out, nand_17_out, nand_18_out);
  nand nand_64 (nand_64_out, nand_19_out, nand_20_out);
  nand nand_65 (nand_65_out, nand_21_out, nand_22_out);
  nand nand_66 (nand_66_out, nand_23_out, nand_24_out);
  nand nand_67 (nand_67_out, nand_25_out, D);
  nand nand_68 (nand_68_out, nand_26_out, nand_27_out);
  nand nand_69 (nand_69_out, C, nand_28_out);
  nand nand_70 (nand_70_out, B, nand_29_out);
  nand nand_71 (nand_71_out, nand_30_out, B);
  nand nand_72 (nand_72_out, D, nand_31_out);
  nand nand_73 (nand_73_out, nand_32_out, nand_33_out);
  nand nand_74 (nand_74_out, C, nand_34_out);
  nand nand_75 (nand_75_out, nand_35_out, C);
  nand nand_76 (nand_76_out, nand_36_out, nand_37_out);
  nand nand_77 (nand_77_out, C, D);
  nand nand_78 (nand_78_out, nand_38_out, B);
  nand nand_79 (nand_79_out, nand_39_out, nand_40_out);
  nand nand_80 (nand_80_out, B, D);
  nand nand_81 (nand_81_out, A, nand_41_out);
  nand nand_82 (nand_82_out, nand_42_out, E);
  nand nand_83 (nand_83_out, nand_43_out, nand_44_out);
  nand nand_84 (nand_84_out, nand_45_out, nand_46_out);
  nand nand_85 (nand_85_out, nand_47_out, nand_48_out);
  nand nand_86 (nand_86_out, nand_49_out, nand_50_out);
  nand nand_87 (nand_87_out, nand_51_out, nand_51_out);
  nand nand_88 (nand_88_out, nand_52_out, nand_52_out);
  nand nand_89 (nand_89_out, E, E);
  nand nand_90 (nand_90_out, nand_53_out, nand_53_out);
  nand nand_91 (nand_91_out, A, A);
  nand nand_92 (nand_92_out, nand_54_out, nand_54_out);
  nand nand_93 (nand_93_out, nand_55_out, nand_55_out);
  nand nand_94 (nand_94_out, nand_56_out, nand_56_out);
  nand nand_95 (nand_95_out, D, D);
  nand nand_96 (nand_96_out, nand_57_out, nand_57_out);
  nand nand_97 (nand_97_out, nand_58_out, nand_58_out);
  nand nand_98 (nand_98_out, nand_59_out, nand_59_out);
  nand nand_99 (nand_99_out, A, A);
  nand nand_100 (nand_100_out, C, C);
  nand nand_101 (nand_101_out, D, D);
  nand nand_102 (nand_102_out, nand_60_out, nand_60_out);
  nand nand_103 (nand_103_out, nand_61_out, nand_61_out);
  nand nand_104 (nand_104_out, nand_62_out, nand_62_out);
  nand nand_105 (nand_105_out, C, C);
  nand nand_106 (nand_106_out, B, B);
  nand nand_107 (nand_107_out, nand_63_out, E);
  nand nand_108 (nand_108_out, B, C);
  nand nand_109 (nand_109_out, nand_64_out, E);
  nand nand_110 (nand_110_out, B, C);
  nand nand_111 (nand_111_out, nand_65_out, E);
  nand nand_112 (nand_112_out, B, C);
  nand nand_113 (nand_113_out, nand_66_out, E);
  nand nand_114 (nand_114_out, B, C);
  nand nand_115 (nand_115_out, nand_67_out, nand_67_out);
  nand nand_116 (nand_116_out, nand_68_out, nand_68_out);
  nand nand_117 (nand_117_out, nand_69_out, nand_69_out);
  nand nand_118 (nand_118_out, B, B);
  nand nand_119 (nand_119_out, D, D);
  nand nand_120 (nand_120_out, E, E);
  nand nand_121 (nand_121_out, nand_70_out, nand_70_out);
  nand nand_122 (nand_122_out, nand_71_out, nand_71_out);
  nand nand_123 (nand_123_out, nand_72_out, nand_72_out);
  nand nand_124 (nand_124_out, C, C);
  nand nand_125 (nand_125_out, nand_73_out, nand_73_out);
  nand nand_126 (nand_126_out, nand_74_out, nand_74_out);
  nand nand_127 (nand_127_out, nand_75_out, nand_75_out);
  nand nand_128 (nand_128_out, nand_76_out, nand_76_out);
  nand nand_129 (nand_129_out, nand_77_out, nand_77_out);
  nand nand_130 (nand_130_out, nand_78_out, nand_78_out);
  nand nand_131 (nand_131_out, nand_79_out, nand_79_out);
  nand nand_132 (nand_132_out, nand_80_out, nand_80_out);
  nand nand_133 (nand_133_out, E, E);
  nand nand_134 (nand_134_out, nand_81_out, nand_81_out);
  nand nand_135 (nand_135_out, nand_82_out, nand_82_out);
  nand nand_136 (nand_136_out, C, C);
  nand nand_137 (nand_137_out, E, E);
  nand nand_138 (nand_138_out, nand_83_out, E);
  nand nand_139 (nand_139_out, nand_84_out, D);
  nand nand_140 (nand_140_out, nand_85_out, E);
  nand nand_141 (nand_141_out, nand_86_out, D);
  nand nand_142 (nand_142_out, nand_87_out, E);
  nand nand_143 (nand_143_out, nand_88_out, nand_89_out);
  nand nand_144 (nand_144_out, nand_90_out, E);
  nand nand_145 (nand_145_out, nand_91_out, C);
  nand nand_146 (nand_146_out, nand_92_out, nand_93_out);
  nand nand_147 (nand_147_out, nand_94_out, nand_95_out);
  nand nand_148 (nand_148_out, A, D);
  nand nand_149 (nand_149_out, nand_96_out, nand_97_out);
  nand nand_150 (nand_150_out, nand_98_out, D);
  nand nand_151 (nand_151_out, nand_99_out, B);
  nand nand_152 (nand_152_out, nand_100_out, nand_101_out);
  nand nand_153 (nand_153_out, nand_102_out, nand_103_out);
  nand nand_154 (nand_154_out, nand_104_out, nand_105_out);
  nand nand_155 (nand_155_out, A, nand_106_out);
  nand nand_156 (nand_156_out, nand_107_out, nand_108_out);
  nand nand_157 (nand_157_out, nand_109_out, nand_110_out);
  nand nand_158 (nand_158_out, C, C);
  nand nand_159 (nand_159_out, nand_111_out, nand_112_out);
  nand nand_160 (nand_160_out, nand_113_out, nand_114_out);
  nand nand_161 (nand_161_out, C, C);
  nand nand_162 (nand_162_out, D, D);
  nand nand_163 (nand_163_out, E, E);
  nand nand_164 (nand_164_out, D, D);
  nand nand_165 (nand_165_out, E, E);
  nand nand_166 (nand_166_out, nand_115_out, E);
  nand nand_167 (nand_167_out, nand_116_out, nand_117_out);
  nand nand_168 (nand_168_out, nand_118_out, C);
  nand nand_169 (nand_169_out, nand_119_out, nand_120_out);
  nand nand_170 (nand_170_out, nand_121_out, E);
  nand nand_171 (nand_171_out, nand_122_out, nand_123_out);
  nand nand_172 (nand_172_out, A, nand_124_out);
  nand nand_173 (nand_173_out, nand_125_out, nand_126_out);
  nand nand_174 (nand_174_out, nand_127_out, nand_128_out);
  nand nand_175 (nand_175_out, nand_129_out, E);
  nand nand_176 (nand_176_out, nand_130_out, nand_131_out);
  nand nand_177 (nand_177_out, nand_132_out, nand_133_out);
  nand nand_178 (nand_178_out, nand_134_out, nand_135_out);
  nand nand_179 (nand_179_out, A, nand_136_out);
  nand nand_180 (nand_180_out, D, nand_137_out);
  nand nand_181 (nand_181_out, nand_138_out, nand_139_out);
  nand nand_182 (nand_182_out, nand_140_out, nand_141_out);
  nand nand_183 (nand_183_out, nand_142_out, nand_143_out);
  nand nand_184 (nand_184_out, nand_144_out, nand_145_out);
  nand nand_185 (nand_185_out, nand_146_out, nand_147_out);
  nand nand_186 (nand_186_out, nand_148_out, nand_148_out);
  nand nand_187 (nand_187_out, E, E);
  nand nand_188 (nand_188_out, nand_149_out, nand_150_out);
  nand nand_189 (nand_189_out, nand_151_out, nand_151_out);
  nand nand_190 (nand_190_out, nand_152_out, nand_152_out);
  nand nand_191 (nand_191_out, nand_153_out, nand_154_out);
  nand nand_192 (nand_192_out, nand_155_out, nand_155_out);
  nand nand_193 (nand_193_out, E, E);
  nand nand_194 (nand_194_out, nand_156_out, nand_157_out);
  nand nand_195 (nand_195_out, A, nand_158_out);
  nand nand_196 (nand_196_out, nand_159_out, nand_160_out);
  nand nand_197 (nand_197_out, A, nand_161_out);
  nand nand_198 (nand_198_out, A, nand_162_out);
  nand nand_199 (nand_199_out, A, nand_163_out);
  nand nand_200 (nand_200_out, A, nand_164_out);
  nand nand_201 (nand_201_out, A, nand_165_out);
  nand nand_202 (nand_202_out, nand_166_out, nand_167_out);
  nand nand_203 (nand_203_out, nand_168_out, nand_168_out);
  nand nand_204 (nand_204_out, nand_169_out, nand_169_out);
  nand nand_205 (nand_205_out, nand_170_out, nand_171_out);
  nand nand_206 (nand_206_out, nand_172_out, nand_172_out);
  nand nand_207 (nand_207_out, D, D);
  nand nand_208 (nand_208_out, nand_173_out, nand_174_out);
  nand nand_209 (nand_209_out, nand_175_out, nand_176_out);
  nand nand_210 (nand_210_out, nand_177_out, nand_178_out);
  nand nand_211 (nand_211_out, nand_179_out, nand_179_out);
  nand nand_212 (nand_212_out, nand_180_out, nand_180_out);
  nand nand_213 (nand_213_out, nand_181_out, nand_182_out);
  nand nand_214 (nand_214_out, A, B);
  nand nand_215 (nand_215_out, nand_183_out, nand_183_out);
  nand nand_216 (nand_216_out, nand_184_out, nand_184_out);
  nand nand_217 (nand_217_out, nand_185_out, nand_185_out);
  nand nand_218 (nand_218_out, nand_186_out, nand_187_out);
  nand nand_219 (nand_219_out, nand_188_out, nand_188_out);
  nand nand_220 (nand_220_out, nand_189_out, nand_190_out);
  nand nand_221 (nand_221_out, nand_191_out, nand_191_out);
  nand nand_222 (nand_222_out, nand_192_out, nand_193_out);
  nand nand_223 (nand_223_out, nand_194_out, nand_195_out);
  nand nand_224 (nand_224_out, nand_196_out, nand_197_out);
  nand nand_225 (nand_225_out, nand_198_out, nand_199_out);
  nand nand_226 (nand_226_out, nand_200_out, nand_201_out);
  nand nand_227 (nand_227_out, nand_202_out, nand_202_out);
  nand nand_228 (nand_228_out, nand_203_out, nand_204_out);
  nand nand_229 (nand_229_out, nand_205_out, nand_205_out);
  nand nand_230 (nand_230_out, nand_206_out, nand_207_out);
  nand nand_231 (nand_231_out, nand_208_out, nand_208_out);
  nand nand_232 (nand_232_out, nand_209_out, nand_209_out);
  nand nand_233 (nand_233_out, nand_210_out, nand_210_out);
  nand nand_234 (nand_234_out, nand_211_out, nand_212_out);
  nand nand_235 (L5, nand_213_out, nand_214_out);
  nand nand_236 (nand_236_out, nand_215_out, nand_216_out);
  nand nand_237 (nand_237_out, nand_217_out, nand_218_out);
  nand nand_238 (nand_238_out, nand_219_out, nand_220_out);
  nand nand_239 (nand_239_out, nand_221_out, nand_222_out);
  nand nand_240 (nand_240_out, nand_223_out, nand_224_out);
  nand nand_241 (nand_241_out, nand_225_out, nand_226_out);
  nand nand_242 (nand_242_out, nand_227_out, nand_228_out);
  nand nand_243 (nand_243_out, nand_229_out, nand_230_out);
  nand nand_244 (nand_244_out, nand_231_out, nand_232_out);
  nand nand_245 (nand_245_out, nand_233_out, nand_234_out);
  nand nand_246 (nand_246_out, nand_236_out, nand_236_out);
  nand nand_247 (nand_247_out, nand_237_out, nand_237_out);
  nand nand_248 (nand_248_out, nand_238_out, nand_238_out);
  nand nand_249 (nand_249_out, nand_239_out, nand_239_out);
  nand nand_250 (L2, nand_240_out, nand_241_out);
  nand nand_251 (nand_251_out, nand_242_out, nand_242_out);
  nand nand_252 (nand_252_out, nand_243_out, nand_243_out);
  nand nand_253 (nand_253_out, nand_244_out, nand_244_out);
  nand nand_254 (nand_254_out, nand_245_out, nand_245_out);
  nand nand_255 (L0, nand_246_out, nand_247_out);
  nand nand_256 (L1, nand_248_out, nand_249_out);
  nand nand_257 (L3, nand_251_out, nand_252_out);
  nand nand_258 (L4, nand_253_out, nand_254_out);
endmodule

module Registrador_De_Letra (
  input  [4:0] Entrada,
  input  Clock,
  input  Reset,
  output out_4,
  output out_5,
  output _6,
  output out_7,
  output _7,
  output out_9
);

  wire [4:0] register_1_q;

  Letras_LED letras_led_1 (
    .A(register_1_q[4]), .B(register_1_q[3]), .C(register_1_q[2]), .D(register_1_q[1]), .E(register_1_q[0]),
    .L0(out_4), .L1(_6), .L2(_7), .L3(out_9), .L4(out_7), .L5(out_5));
  Register #(.width(5), .trigger("high")) register_1 (
    .D(Entrada), .Q(register_1_q), .clk(Clock), .clr(Reset));  // open: en
endmodule

module Conversor_8X5 (
  input  [6:0] in_1,
  output [4:0] out_2
);


  assign out_2 = in_1[4:0];

  // Notes on the sheet:
  //   5
endmodule

module Codificador_De_32_Letras (
  input  [4:0] in_1,
  output out_2
);

  wire decoder_1_out0, decoder_1_out1, decoder_1_out2, decoder_1_out3, decoder_1_out4, decoder_1_out5,
       decoder_1_out6, decoder_1_out7, decoder_1_out8, decoder_1_out9, decoder_1_out10, decoder_1_out11,
       decoder_1_out12, decoder_1_out13, decoder_1_out14, decoder_1_out15, decoder_1_out16, decoder_1_out17,
       decoder_1_out18, decoder_1_out19, decoder_1_out20, decoder_1_out21, decoder_1_out22, decoder_1_out23,
       decoder_1_out24, decoder_1_out25, decoder_1_out26, decoder_1_out27, decoder_1_out28, decoder_1_out29,
       decoder_1_out30, decoder_1_out31;

  Decoder #(.select(5)) decoder_1 (
    .out0(decoder_1_out0), .out1(decoder_1_out1), .out2(decoder_1_out2), .out3(decoder_1_out3),
    .out4(decoder_1_out4), .out5(decoder_1_out5), .out6(decoder_1_out6), .out7(decoder_1_out7),
    .out8(decoder_1_out8), .out9(decoder_1_out9), .out10(decoder_1_out10), .out11(decoder_1_out11),
    .out12(decoder_1_out12), .out13(decoder_1_out13), .out14(decoder_1_out14), .out15(decoder_1_out15),
    .out16(decoder_1_out16), .out17(decoder_1_out17), .out18(decoder_1_out18), .out19(decoder_1_out19),
    .out20(decoder_1_out20), .out21(decoder_1_out21), .out22(decoder_1_out22), .out23(decoder_1_out23),
    .out24(decoder_1_out24), .out25(decoder_1_out25), .out26(decoder_1_out26), .out27(decoder_1_out27),
    .out28(decoder_1_out28), .out29(decoder_1_out29), .out30(decoder_1_out30), .out31(decoder_1_out31),
    .sel(in_1));  // open: en
  or or_1 (out_2, decoder_1_out0, decoder_1_out1, decoder_1_out2, decoder_1_out3, decoder_1_out4, decoder_1_out5, decoder_1_out6, decoder_1_out7, decoder_1_out8, decoder_1_out9, decoder_1_out10, decoder_1_out11, decoder_1_out12, decoder_1_out13, decoder_1_out14, decoder_1_out15, decoder_1_out16, decoder_1_out17, decoder_1_out18, decoder_1_out19, decoder_1_out20, decoder_1_out21, decoder_1_out22, decoder_1_out23, decoder_1_out24, decoder_1_out25, decoder_1_out26, decoder_1_out27, decoder_1_out28, decoder_1_out29, decoder_1_out30, decoder_1_out31);
endmodule
