// Logisim project Conversor De Braile-Letra.circ as structural Verilog: 1 circuit, main circuit main
module main (
  input  _1,
  input  _2,
  input  _3,
  input  in_4,
  input  in_5,
  input  in_6,
  input  in_7
);

  wire Clear, Enter;
  wire [6:0] rom_1_data;

  Button button_1 (.out(Enter));
  Button button_2 (.out(Clear));
  ROM #(.addrWidth(6), .dataWidth(7)) rom_1 (.addr({_3, in_5, in_7, in_6, in_4, _2}), .data(rom_1_data), .sel(_1));
  TTY tty_1 (.data(rom_1_data), .clk(Enter), .clr(Clear));  // open: we

  // Other names for the same wires on the sheet: On_Off = _1

  // Notes on the sheet:
  //   4
  //   6
  //   contents of rom_1 (hex, n*v repeats v):
  //   20 41 0 42 0 4b 0 4c 5*0 55 0 56 0 45 0 48 0 4f 0 52 5*0 5a 0 0 0 43 49 46 0 4d 53 50 5*0 58 0 0 0
  //   44 4a 47 0 4e 54 51 0 0 57 0 0 59
  //   5
endmodule
